# Fritzing sketch veri-cleanse-poc4 (saved by Fritzing 0.9.4)
breadboards: 1

parts:
  U1 = ESP32S-HiLetgo [part_number=ESP32S-HiLetgo]
  LED1 = LED - 5mm [color="Red (633nm)" package="5 mm [THT]"]
  U2 = RELAY [package=relay-jzc]
  VCC1 = 4 x AAA Battery Mount  # not connected
  M1 = DC Motor

nets:
  N1: U1.GPIO26, U2.COIL1
  N2: U1.GPIO27, LED1.anode
  N3: U1.GND, LED1.cathode, U2.MAIN
  N4: U2.NO, M1.pin_1

custom parts:
  ESP32S-HiLetgo: HiLetgo ESP-WROOM-32 ESP32 ESP-32S Development Board 2.4GHz Dual-Mode WiFi + Bluetooth Dual Cores Microcontroller The ESP32 integrated with Antenna switches, RF Balun, power amplifiers, low-noise amplifiers, filters, and management modules, and the entire solution occupies the least area of PCB. 2.4 GHz Wi-Fi plus Bluetooth dual-mode chip, with TSMC Ultra-low power consumption 40nm technology,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
